# Fritzing sketch motor-brake (saved by Fritzing 0.9.2b)
breadboards: 1

parts:
  M1 = DC Motor
  D1 = Diode [package=diode-1n4001]
  D2 = Diode [package=diode-1n4001]
  VCC1 = Battery
  Part1 = Arduino Nano (Rev3.0) (ICSP)
  Q1 = Basic FET N-Channel [package="TO220 [THT]"]
  Q2 = Basic FET N-Channel [package="TO220 [THT]"]

nets:
  N1: M1.pin_1, M1.pin_2, D1.C, D2.C, VCC1.-
  N2: VCC1.+, Q1.source, Q2.source
  N3: Part1.D3, Q1.gate
  N4: Part1.D4, Q2.gate
